# Fritzing sketch icof (saved by Fritzing 0.9.9b)
breadboards: 1

parts:
  Raspberry_Pi_1 = Raspberry Pi 3 [part_number=RPI-3-V1.2]
  R1 = Resistor [tolerance=±5% power=0.25 resistance=10k package=THT]
  S1 = Square Pushbutton

nets:
  N1: Raspberry_Pi_1.3v3, S1.leg0
  N2: Raspberry_Pi_1.GPIO3, Raspberry_Pi_1.GND, R1.Pin_0
  N3: Raspberry_Pi_1.GPIO17, R1.Pin_1, S1.leg1
